# Fritzing sketch led (saved by Fritzing 0.9.0b)
breadboards: 1

parts:
  Part1 = Spark Core (v1.0)
  R4 = Resistor [tolerance=±5% resistance=1k package="0603 [SMD]"]
  R5 = Resistor [tolerance=±5% resistance=1k package="0603 [SMD]"]
  R6 = Resistor [tolerance=±5% resistance=1k package="0603 [SMD]"]
  LED1 = RGB LED (com. cathode, rbg) [package="5 mm [THT]"]

nets:
  N1: Part1.A5, R4.Pin_0
  N2: Part1.A6, R5.Pin_0
  N3: Part1.A7, R6.Pin_0
  N4: Part1.GND, LED1.blue_anode
  N5: R4.Pin_1, LED1.green_anode
  N6: R5.Pin_1, LED1.common_cathode
  N7: R6.Pin_1, LED1.red_anode
