# Fritzing sketch proximity (saved by Fritzing 0.9.0b)
breadboards: 1

parts:
  U1 = HC-SR04 [chip_label=IC package="SIP (Single Inline) [THT]"]
  Part1 = Spark Core (v1.0)

nets:
  VCC: U1.Vcc, Part1.VIN
  N1: U1.Trig, Part1.D4
  N2: U1.Echo, Part1.D5
  GND: U1.GND, Part1.GND

custom parts:
  HC-SR04: HC-SR04 ultrasound distance sensor
